# Fritzing sketch kamigami (saved by Fritzing 0.9.4)

parts:
  MCU1 = Raspberry Pi Zero
  Part1 = Motor Driver 1A Dual TB6612FNG
  Part2 = Adafruit LSM6DS33 6-DoF Accel + Gyro IMU [part_number="Adafruit #4480"]
  M1 = DC Motor
  M2 = DC Motor
  BATT1 = LiPoly Battery (1300mAh)  # not connected
  Part3 = Adafruit Switched JST Breakout [part_number="Adafruit #1863"]

nets:
  VCC: MCU1.pin_1, Part2.VCC, Part2.3.3V
  N1: MCU1.pin_2, MCU1.pin_4, Part3.V+
  N2: MCU1.pin_3, Part2.SDA, Part2.INT1
  N3: MCU1.pin_5, Part2.SCL
  GND: MCU1.pin_6, MCU1.pin_9, MCU1.pin_20, Part1.GND, Part2.GND, Part3.GND
  N4: MCU1.pin_11, Part1.STBY
  N5: MCU1.pin_12, Part1.PWMB
  N6: MCU1.pin_13, Part1.AIN1
  N7: MCU1.pin_15, Part1.AIN2
  N8: MCU1.pin_16, Part1.BIN1
  N9: MCU1.pin_18, Part1.BIN2
  N10: MCU1.pin_33, Part1.PWMA
  N11: Part1.B01, M1.pin_2
  N12: Part1.B02, M1.pin_1
  N13: Part1.A02, M2.pin_1
  N14: Part1.A01, M2.pin_2
  N15: Part1.VCC, Part1.VM, Part3.SW

custom parts:
  Adafruit LSM6DS33 6-DoF Accel + Gyro IMU: Add motion and orientation sensing to your Arduino project with this affordable 6 Degree of Freedom (6-DoF) sensor with sensors from ST. The board includes an LSM6DS33, a 6-DoF IMU accelerometer + gyro. The 3-axis accelerometer, can tell you which direction is down towards the Earth (by measuring gravity) or how fast the board is accelerating in 3D space. The 3-axis gyroscope that can measure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
  LiPoly Battery (1300mAh): Lithium Ion Polymer Battery (1300mAh)
  Adafruit Switched JST Breakout: This switched JST connector is the best way to quickly prototype with our LiPoly batteries. We paired a genuine JST connector with a slide switch that can do up to 600mA. Both are soldered onto a breadboard-friendly breakout. There's two ground pins, one 'switched' power pin, and one pin that is always on. This is compatible with the "JST PH 2-pin" connectors we use in our battery packs..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
